# Fritzing sketch airgoblin (saved by Fritzing 0.8.3b)
breadboards: 1

parts:
  nRF24L01+ = QFN-20-0.4MM [package=QFN]
  XTAL1 = CRYSTAL - kHz [frequency="16 Mhz"]
  C1 = Ceramic Capacitor [capacitance=10nF package="0603 [SMD, multilayer]"]
  C2 = Ceramic Capacitor [capacitance=1nF package="0603 [SMD, multilayer]"]
  C3 = Ceramic Capacitor [capacitance=22pF package="0603 [SMD, multilayer]"]
  L1 = Inductor [inductance=2.7nH package="400 mil [THT]"]
  C5 = Ceramic Capacitor [capacitance=100nF package="100 mil [THT, multilayer]"]
  C6 = Ceramic Capacitor [capacitance=100nF package="100 mil [THT, multilayer]"]
  L2 = Inductor [inductance=8.2nH package="400 mil [THT]"]
  L3 = Inductor [inductance=3.9nH package="400 mil [THT]"]
  C7 = Ceramic Capacitor [capacitance=1.5pF package="100 mil [THT, multilayer]"]
  C8 = Ceramic Capacitor [capacitance=1pF package="100 mil [THT, multilayer]"]
  C9 = Ceramic Capacitor [capacitance=33nF package="0603 [SMD, multilayer]"]
  R1 = Resistor [tolerance=±5% package="0402 [SMD]"]
  R2 = Resistor [tolerance=±5% package="0402 [SMD]"]
  C4 = Ceramic Capacitor [capacitance=22pF package="0603 [SMD, multilayer]"]

nets:
  CE: nRF24L01+.1
  CSN: nRF24L01+.2
  SCK: nRF24L01+.3
  MOSI: nRF24L01+.4
  MISO: nRF24L01+.5
  IRQ: nRF24L01+.6
  3.3V: nRF24L01+.7, nRF24L01+.15, nRF24L01+.18, C1.1, C2.1
  GND: nRF24L01+.8, nRF24L01+.14, nRF24L01+.17, nRF24L01+.20, C3.0, C5.0, C6.0, C8.0, R2.Pin_1, C4.0
  N1: nRF24L01+.9, XTAL1.pin_0, C3.1, R1.Pin_0
  N2: nRF24L01+.10, XTAL1.pin_1, R1.Pin_1, C4.1
  N3: nRF24L01+.11, L1.pin_1, C5.1, C6.1
  N4: nRF24L01+.12, L1.pin_0, L2.pin_1
  N5: nRF24L01+.13, L2.pin_0, L3.pin_0
  N6: nRF24L01+.16, R2.Pin_0
  N7: nRF24L01+.19, C9.1
  N8: L3.pin_1, C7.1
  50 Ohm RF Out: C7.0, C8.1
